// Logisim project adder4b.circ as structural Verilog: 4 circuits, main circuit main
module main (
  input  a3,
  input  a2,
  input  a1,
  input  a0,
  input  c0,
  input  b3,
  input  b2,
  input  b1,
  input  b0,
  output c4
);

  wire bin2hex_1_s, bin2hex_1_u, bin2hex_1_v, bin2hex_1_x, bin2hex_1_y, bin2hex_1_z, bin2hex_2_s,
       bin2hex_2_u, bin2hex_2_v, bin2hex_2_w, bin2hex_2_x, bin2hex_2_y, bin2hex_2_z, bin2hex_3_s,
       bin2hex_3_u, bin2hex_3_v, bin2hex_3_w, bin2hex_3_x, bin2hex_3_y, bin2hex_3_z, cla_1_s0, cla_1_s1,
       cla_1_s2, cla_1_s3;

  bin2hex bin2hex_1 (
    .a(a3), .b(a2), .c(a1), .d(a0), .x(bin2hex_1_x), .y(bin2hex_1_y), .z(bin2hex_1_z), .u(bin2hex_1_u),
    .v(bin2hex_1_v), .w(bin2hex_1_v), .s(bin2hex_1_s));
  bin2hex bin2hex_2 (
    .a(b3), .b(b2), .c(b1), .d(b0), .x(bin2hex_2_x), .y(bin2hex_2_y), .z(bin2hex_2_z), .u(bin2hex_2_u),
    .v(bin2hex_2_v), .w(bin2hex_2_w), .s(bin2hex_2_s));
  _7_Segment_Display u_7_segment_display_1 (
    .g(bin2hex_1_s), .f(bin2hex_1_v), .a(bin2hex_1_x), .b(bin2hex_1_y), .e(bin2hex_1_v), .d(bin2hex_1_u),
    .c(bin2hex_1_z));  // open: dp
  _7_Segment_Display u_7_segment_display_2 (
    .g(bin2hex_2_s), .f(bin2hex_2_w), .a(bin2hex_2_x), .b(bin2hex_2_y), .e(bin2hex_2_v), .d(bin2hex_2_u),
    .c(bin2hex_2_z));  // open: dp
  CLA cla_1 (
    .b3(b3), .a3(a3), .b2(b2), .a2(a2), .b1(b1), .a1(a1), .b0(b0), .a0(a0), .c0(c0), .c4(c4), .s3(cla_1_s3),
    .s2(cla_1_s2), .s1(cla_1_s1), .s0(cla_1_s0));
  bin2hex bin2hex_3 (
    .a(cla_1_s3), .b(cla_1_s2), .c(cla_1_s1), .d(cla_1_s0), .x(bin2hex_3_x), .y(bin2hex_3_y),
    .z(bin2hex_3_z), .u(bin2hex_3_u), .v(bin2hex_3_v), .w(bin2hex_3_w), .s(bin2hex_3_s));
  _7_Segment_Display u_7_segment_display_3 (
    .g(bin2hex_3_s), .f(bin2hex_3_w), .a(bin2hex_3_x), .b(bin2hex_3_y), .e(bin2hex_3_v), .d(bin2hex_3_u),
    .c(bin2hex_3_z));  // open: dp
endmodule

module cla (
  input  in_1,
  input  in_2,
  input  in_3,
  input  in_4,
  input  in_5,
  input  in_6,
  input  in_7,
  input  in_8,
  input  in_9,
  output out_10,
  output out_11,
  output out_12
);

  wire and_1_out, and_2_out, and_3_out, and_4_out, and_5_out, and_6_out, or_1_out, or_2_out, xor_1_out,
       xor_2_out, xor_3_out, xor_4_out;

  and and_1 (and_1_out, in_2, in_3);
  xor xor_1 (xor_1_out, in_2, in_3);
  and and_2 (and_2_out, in_4, in_5);
  xor xor_2 (xor_2_out, in_4, in_5);
  and and_3 (and_3_out, in_6, in_7);
  xor xor_3 (xor_3_out, in_6, in_7);
  and and_4 (and_4_out, in_8, in_9);
  xor xor_4 (xor_4_out, in_8, in_9);
  xor xor_5 (out_10, in_1, xor_1_out);
  and and_5 (and_5_out, xor_1_out, in_1);
  and and_6 (and_6_out, xor_1_out, xor_2_out, in_1);
  or or_1 (or_1_out, and_5_out, and_1_out);
  or or_2 (or_2_out, and_6_out, and_2_out);
  xor xor_6 (out_11, or_1_out, xor_2_out);
  xor xor_7 (out_12, or_2_out, xor_3_out);
endmodule

module bin2hex (
  input  a,
  input  b,
  input  c,
  input  d,
  output x,
  output y,
  output z,
  output u,
  output v,
  output w,
  output s
);

  wire and_1_out, and_2_out, and_3_out, and_4_out, and_5_out, and_6_out, and_7_out, and_8_out, and_9_out,
       and_10_out, and_11_out, and_12_out, and_13_out, and_14_out, and_15_out, and_16_out, and_17_out,
       and_18_out, and_19_out, and_20_out, and_21_out, and_22_out, and_23_out, and_24_out, and_25_out,
       and_26_out, and_27_out, and_28_out, and_29_out, and_30_out, and_31_out, and_32_out, and_33_out,
       and_34_out, and_35_out, and_36_out, not_1_out, not_2_out, not_3_out, not_4_out, not_5_out, not_6_out,
       not_7_out, not_8_out, not_9_out, not_10_out, not_11_out, not_12_out, not_13_out, not_14_out,
       not_15_out, not_16_out, not_17_out, not_18_out, not_19_out, not_20_out, not_21_out, not_22_out,
       not_23_out, not_24_out, not_25_out, not_26_out, not_27_out, not_28_out, not_29_out, not_30_out,
       not_31_out, not_32_out, not_33_out, not_34_out, not_35_out, not_36_out, not_37_out, not_38_out,
       not_39_out, not_40_out, not_41_out, not_42_out, not_43_out, not_44_out;

  not not_1 (not_1_out, b);
  and and_1 (and_1_out, not_1_out, not_2_out);
  not not_2 (not_2_out, d);
  not not_3 (not_3_out, a);
  and and_2 (and_2_out, not_3_out, c);
  not not_4 (not_4_out, a);
  and and_3 (and_3_out, not_4_out, b, d);
  and and_4 (and_4_out, b, c);
  not not_5 (not_5_out, b);
  and and_5 (and_5_out, a, not_5_out, not_6_out);
  not not_6 (not_6_out, c);
  and and_6 (and_6_out, a, not_7_out);
  not not_7 (not_7_out, d);
  not not_8 (not_8_out, a);
  and and_7 (and_7_out, not_8_out, not_9_out);
  not not_9 (not_9_out, b);
  not not_10 (not_10_out, a);
  and and_8 (and_8_out, not_10_out, not_11_out, not_12_out);
  not not_11 (not_11_out, c);
  not not_12 (not_12_out, d);
  not not_13 (not_13_out, b);
  and and_9 (and_9_out, not_13_out, not_14_out);
  not not_14 (not_14_out, c);
  not not_15 (not_15_out, b);
  and and_10 (and_10_out, not_15_out, not_16_out);
  not not_16 (not_16_out, d);
  not not_17 (not_17_out, a);
  and and_11 (and_11_out, not_17_out, c, d);
  and and_12 (and_12_out, a, not_18_out, d);
  not not_18 (not_18_out, c);
  not not_19 (not_19_out, a);
  and and_13 (and_13_out, not_19_out, not_20_out);
  not not_20 (not_20_out, c);
  not not_21 (not_21_out, a);
  and and_14 (and_14_out, not_21_out, d);
  not not_22 (not_22_out, c);
  and and_15 (and_15_out, not_22_out, d);
  not not_23 (not_23_out, a);
  and and_16 (and_16_out, not_23_out, b);
  and and_17 (and_17_out, a, not_24_out);
  not not_24 (not_24_out, b);
  not not_25 (not_25_out, b);
  and and_18 (and_18_out, not_25_out, not_26_out);
  not not_26 (not_26_out, d);
  not not_27 (not_27_out, b);
  and and_19 (and_19_out, not_27_out, c);
  and and_20 (and_20_out, c, not_28_out);
  not not_28 (not_28_out, d);
  not not_29 (not_29_out, c);
  and and_21 (and_21_out, b, not_29_out, d);
  and and_22 (and_22_out, a, not_30_out);
  not not_30 (not_30_out, c);
  not not_31 (not_31_out, b);
  and and_23 (and_23_out, not_31_out, not_32_out);
  not not_32 (not_32_out, d);
  and and_24 (and_24_out, c, not_33_out);
  not not_33 (not_33_out, d);
  and and_25 (and_25_out, a, c);
  and and_26 (and_26_out, a, b);
  not not_34 (not_34_out, c);
  and and_27 (and_27_out, not_34_out, not_35_out);
  not not_35 (not_35_out, d);
  not not_36 (not_36_out, a);
  and and_28 (and_28_out, not_36_out, b, not_37_out);
  not not_37 (not_37_out, c);
  and and_29 (and_29_out, b, not_38_out);
  not not_38 (not_38_out, d);
  not not_39 (not_39_out, b);
  and and_30 (and_30_out, a, not_39_out, d);
  and and_31 (and_31_out, a, b, c);
  not not_40 (not_40_out, b);
  and and_32 (and_32_out, not_40_out, c);
  and and_33 (and_33_out, c, not_41_out);
  not not_41 (not_41_out, d);
  not not_42 (not_42_out, a);
  and and_34 (and_34_out, not_42_out, b, not_43_out);
  not not_43 (not_43_out, c);
  and and_35 (and_35_out, a, not_44_out);
  not not_44 (not_44_out, b);
  and and_36 (and_36_out, a, d);
  or or_1 (z, and_13_out, and_14_out, and_15_out, and_16_out, and_17_out);
  or or_2 (u, and_18_out, and_19_out, and_20_out, and_21_out, and_22_out);
  or or_3 (v, and_23_out, and_24_out, and_25_out, and_26_out);
  or or_4 (w, and_27_out, and_28_out, and_29_out, and_30_out, and_31_out);
  or or_5 (s, and_32_out, and_33_out, and_34_out, and_35_out, and_36_out);
  or or_6 (x, and_1_out, and_2_out, and_3_out, and_4_out, and_5_out, and_6_out);
  or or_7 (y, and_7_out, and_8_out, and_9_out, and_10_out, and_11_out, and_12_out);
endmodule

module CLA (
  input  b3,
  input  a3,
  input  b2,
  input  a2,
  input  b1,
  input  a1,
  input  b0,
  input  a0,
  input  c0,
  output c4,
  output s3,
  output s2,
  output s1,
  output s0
);

  wire and_1_out, and_2_out, and_3_out, and_4_out, and_5_out, and_6_out, and_7_out, and_8_out, and_9_out,
       and_10_out, and_11_out, and_12_out, and_13_out, and_14_out, nand_1_out, nand_2_out, nand_3_out,
       nand_4_out, nor_1_out, nor_2_out, nor_3_out, nor_4_out, nor_5_out, nor_6_out, nor_8_out, not_1_out,
       not_2_out, not_3_out, not_4_out, not_5_out, not_6_out;

  nand nand_1 (nand_1_out, b3, a3);
  nor nor_1 (nor_1_out, b3, a3);
  not not_1 (not_1_out, c0);
  nand nand_2 (nand_2_out, b2, a2);
  nor nor_2 (nor_2_out, b2, a2);
  nand nand_3 (nand_3_out, b1, a1);
  nor nor_3 (nor_3_out, b1, a1);
  nand nand_4 (nand_4_out, b0, a0);
  nor nor_4 (nor_4_out, b0, a0);
  not not_2 (not_2_out, nor_4_out);
  not not_3 (not_3_out, not_1_out);
  not not_4 (not_4_out, nor_1_out);
  not not_5 (not_5_out, nor_2_out);
  not not_6 (not_6_out, nor_3_out);
  and and_1 (and_1_out, nand_4_out, not_2_out);
  and and_2 (and_2_out, nor_2_out, nand_1_out);
  and and_3 (and_3_out, nor_3_out, nand_1_out, nand_2_out);
  and and_4 (and_4_out, nor_4_out, nand_1_out, nand_2_out, nand_3_out);
  and and_5 (and_5_out, nand_1_out, nand_2_out, nand_3_out, nand_4_out, not_1_out);
  and and_6 (and_6_out, nand_1_out, not_4_out);
  and and_7 (and_7_out, nor_3_out, nand_2_out);
  and and_8 (and_8_out, nor_4_out, nand_2_out, nand_3_out);
  and and_9 (and_9_out, nand_2_out, nand_3_out, nand_4_out, not_1_out);
  and and_10 (and_10_out, nand_2_out, not_5_out);
  and and_11 (and_11_out, nor_4_out, nand_3_out);
  and and_12 (and_12_out, nand_3_out, nand_4_out, not_1_out);
  and and_13 (and_13_out, nand_3_out, not_6_out);
  and and_14 (and_14_out, nand_4_out, not_1_out);
  nor nor_5 (nor_5_out, and_11_out, nor_3_out, and_12_out);
  nor nor_6 (nor_6_out, nor_4_out, and_14_out);
  xor xor_1 (s0, and_1_out, not_3_out);
  nor nor_7 (c4, and_2_out, and_3_out, nor_1_out, and_4_out, and_5_out);
  nor nor_8 (nor_8_out, and_7_out, nor_2_out, and_8_out, and_9_out);
  xor xor_2 (s2, and_10_out, nor_5_out);
  xor xor_3 (s3, and_6_out, nor_8_out);
  xor xor_4 (s1, and_13_out, nor_6_out);
endmodule
