// Logisim project fulladder.circ as structural Verilog: 2 circuits, main circuit main
module main (
  input  a0,
  input  b0,
  input  ci0,
  output s0,
  output co0
);

  wire and_1_out, and_2_out, xor_1_out;

  xor xor_1 (xor_1_out, a0, b0);
  and and_1 (and_1_out, a0, b0);
  xor xor_2 (s0, xor_1_out, ci0);
  and and_2 (and_2_out, xor_1_out, ci0);
  or or_1 (co0, and_1_out, and_2_out);
endmodule

module _4bits (
  input  ci0,
  input  a0,
  input  b0,
  input  a1,
  input  b1,
  input  a2,
  input  b2,
  input  a3,
  input  b3,
  output s0,
  output s1,
  output s2,
  output s3,
  output co3
);

  wire main_1_co0, main_2_co0, main_3_co0;

  main main_1 (.a0(a0), .b0(b0), .ci0(ci0), .s0(s0), .co0(main_1_co0));
  main main_2 (.a0(a1), .b0(b1), .ci0(main_1_co0), .s0(s1), .co0(main_2_co0));
  main main_3 (.a0(a2), .b0(b2), .ci0(main_2_co0), .s0(s2), .co0(main_3_co0));
  main main_4 (.a0(a3), .b0(b3), .ci0(main_3_co0), .s0(s3), .co0(co3));
endmodule
