// Logisim project mux.circ as structural Verilog: 3 circuits, main circuit main
module main (
  input  op1,
  input  op0,
  input  e0,
  input  e1,
  input  e2,
  input  e3,
  output s
);

  wire and_1_out, and_2_out, and_3_out, and_4_out, not_1_out, not_2_out, not_3_out, not_4_out;

  not not_1 (not_1_out, op0);
  not not_2 (not_2_out, op1);
  not not_3 (not_3_out, op1);
  not not_4 (not_4_out, op0);
  and and_1 (and_1_out, e0, not_1_out, not_2_out);
  and and_2 (and_2_out, e1, op0, not_3_out);
  and and_3 (and_3_out, e2, not_4_out, op1);
  and and_4 (and_4_out, e3, op0, op1);
  or or_1 (s, and_1_out, and_2_out, and_3_out, and_4_out);
endmodule

module alu (
  input  binv,
  input  ci,
  input  a,
  input  op1,
  input  op0,
  input  b,
  output s0,
  output co
);

  wire adder_1_out, and_1_out, and_2_out, and_3_out, not_1_out, not_2_out, not_3_out, or_1_out, or_2_out;

  not not_1 (not_1_out, binv);
  not not_2 (not_2_out, b);
  and and_1 (and_1_out, not_1_out, b);
  and and_2 (and_2_out, binv, not_2_out);
  or or_1 (or_1_out, and_1_out, and_2_out);
  not not_3 (not_3_out, a);
  Adder #(.width(1)) adder_1 (.a(a), .b(or_1_out), .out(adder_1_out), .cin(ci), .cout(co));
  and and_3 (and_3_out, a, or_1_out);
  or or_2 (or_2_out, a, or_1_out);
  main main_1 (.e0(and_3_out), .e1(or_2_out), .e2(not_3_out), .e3(adder_1_out), .op1(op1), .op0(op0), .s(s0));
endmodule

module alu4b (
  input  b3,
  input  b2,
  input  b1,
  input  b0,
  input  a3,
  input  a2,
  input  a1,
  input  a0,
  input  binv,
  input  op1,
  input  op0,
  output s0,
  output s1,
  output s2,
  output s3,
  output cout
);

  wire alu_1_co, alu_2_co, alu_3_co;

  alu alu_1 (.a(a0), .b(b0), .binv(binv), .ci(binv), .op1(op1), .op0(op0), .co(alu_1_co), .s0(s0));
  alu alu_2 (.a(a1), .b(b1), .binv(binv), .ci(alu_1_co), .op1(op1), .op0(op0), .co(alu_2_co), .s0(s1));
  alu alu_3 (.a(a2), .b(b2), .binv(binv), .ci(alu_2_co), .op1(op1), .op0(op0), .co(alu_3_co), .s0(s2));
  alu alu_4 (.a(a3), .b(b3), .binv(binv), .ci(alu_3_co), .op1(op1), .op0(op0), .co(cout), .s0(s3));
endmodule
